// Logisim project a quadrado.circ as structural Verilog: 11 circuits, main circuit a
module led (
  input  [3:0] in_1,
  input  Cint,
  input  [3:0] in_3,
  output Cout,
  output out_5,
  output out_6,
  output out_7,
  output OVERFLOW
);

  wire decodificador_1_a_2, decodificador_1_b_2, decodificador_1_c_2, decodificador_1_d_2, decodificador_1_e,
       decodificador_1_f, decodificador_1_g, decodificador_1_sinal, somador_1_rs4;

  somador somador_1 (
    .A_prime_prime_prime_prime(in_1[3]), .B_prime_prime_prime_prime(in_3[3]), .A_prime_prime_prime(in_1[2]),
    .B_prime_prime_prime(in_3[2]), .A_prime_prime(in_1[1]), .B_prime_prime(in_3[1]), .A(in_1[0]),
    .B(in_3[0]), .Cout(Cout), .RS4(somador_1_rs4), .RS3(out_5), .RS2(out_6), .RS1(out_7), .overflow(OVERFLOW));
  decodificador decodificador_1 (
    .A(somador_1_rs4), .B(out_5), .C(out_6), .D(out_7), .sinal(decodificador_1_sinal),
    .a_2(decodificador_1_a_2), .b_2(decodificador_1_b_2), .c_2(decodificador_1_c_2),
    .d_2(decodificador_1_d_2), .e(decodificador_1_e), .f(decodificador_1_f), .g(decodificador_1_g));
  _7_Segment_Display u_7_segment_display_1 (
    .g(decodificador_1_g), .f(decodificador_1_f), .a(decodificador_1_a_2), .b(decodificador_1_b_2),
    .e(decodificador_1_e), .d(decodificador_1_d_2), .c(decodificador_1_c_2), .dp(decodificador_1_sinal));
endmodule

module decodificador (
  input  A,
  input  B,
  input  C,
  input  D,
  output sinal,
  output a_2,
  output b_2,
  output c_2,
  output d_2,
  output e,
  output f,
  output g
);

  a a_1 (.A(A), .B(B), .C(C), .D(D), .a_2(a_2));
  b b_1 (.A(A), .B(B), .C(C), .D(D), .b_2(b_2));
  c c_1 (.A(A), .B(B), .C(C), .D(D), .c_2(c_2));
  d d_1 (.B(B), .C(C), .D(D), .d_2(d_2));
  e e_1 (.B(B), .C(C), .D(D), .e(e));
  f f_1 (.A(A), .B(B), .C(C), .D(D), .f(f));
  g g_1 (.A(A), .B(B), .C(C), .D(D), .g(g));

  assign sinal = A;
endmodule

module a (
  input  A,
  input  B,
  input  C,
  input  D,
  output a_2
);

  wire and_1_out, and_2_out, and_3_out, and_4_out, and_5_out;

  and and_1 (and_1_out, A, ~B);  // AND_Gate
  and and_2 (and_2_out, C, ~D);  // AND_Gate
  and and_3 (and_3_out, ~A, C);  // AND_Gate
  and and_4 (and_4_out, B, ~C, D);  // AND_Gate
  and and_5 (and_5_out, ~B, ~D);  // AND_Gate
  or or_1 (a_2, and_1_out, and_2_out, and_3_out, and_4_out, and_5_out);
endmodule

module b (
  input  A,
  input  B,
  input  C,
  input  D,
  output b_2
);

  wire and_1_out, and_2_out, and_3_out, and_4_out, and_5_out;

  and and_1 (and_1_out, A, B);
  and and_2 (and_2_out, ~C, ~D);  // AND_Gate
  and and_3 (and_3_out, ~A, ~B);  // AND_Gate
  and and_4 (and_4_out, ~A, C, D);  // AND_Gate
  and and_5 (and_5_out, A, ~C);  // AND_Gate
  or or_1 (b_2, and_1_out, and_2_out, and_3_out, and_4_out, and_5_out);
endmodule

module c (
  input  A,
  input  B,
  input  C,
  input  D,
  output c_2
);

  wire and_1_out, and_2_out;

  and and_1 (and_1_out, ~A, B);  // AND_Gate
  and and_2 (and_2_out, A, ~B);  // AND_Gate
  or or_1 (c_2, and_1_out, and_2_out, ~C, D);  // OR_Gate
endmodule

module d (
  input  B,
  input  C,
  input  D,
  output d_2
);

  wire and_1_out, and_2_out, and_3_out, and_4_out;

  and and_1 (and_1_out, B, ~C, D);  // AND_Gate
  and and_2 (and_2_out, ~D, C);  // AND_Gate
  and and_3 (and_3_out, ~B, ~D);  // AND_Gate
  and and_4 (and_4_out, ~B, C);  // AND_Gate
  or or_1 (d_2, and_1_out, and_2_out, and_3_out, and_4_out);
endmodule

module e (
  input  B,
  input  C,
  input  D,
  output e
);

  wire and_1_out, and_2_out;

  and and_1 (and_1_out, C, ~D);  // AND_Gate
  and and_2 (and_2_out, ~B, ~D);  // AND_Gate
  or or_1 (e, and_1_out, and_2_out);
endmodule

module f (
  input  A,
  input  B,
  input  C,
  input  D,
  output f
);

  wire and_1_out, and_2_out, and_3_out, and_4_out;

  and and_1 (and_1_out, A, ~B, C);  // AND_Gate
  and and_2 (and_2_out, ~A, B, ~C);  // AND_Gate
  and and_3 (and_3_out, ~A, B, ~D);  // AND_Gate
  and and_4 (and_4_out, ~C, ~D);  // AND_Gate
  or or_1 (f, and_1_out, and_2_out, and_3_out, and_4_out);
endmodule

module g (
  input  A,
  input  B,
  input  C,
  input  D,
  output g
);

  wire and_1_out, and_2_out, and_3_out, and_4_out;

  and and_1 (and_1_out, A, ~D);  // AND_Gate
  and and_2 (and_2_out, B, ~C);  // AND_Gate
  and and_3 (and_3_out, ~B, C);  // AND_Gate
  and and_4 (and_4_out, C, ~D);  // AND_Gate
  or or_1 (g, and_1_out, and_2_out, and_3_out, and_4_out);
endmodule

module full (
  input  A,
  input  B,
  input  Cint,
  output Cout,
  output S
);

  wire and_1_out, and_2_out, and_3_out, and_4_out, and_5_out, and_6_out, and_7_out, not_1_out, not_2_out,
       not_3_out, not_4_out, not_5_out, not_6_out;

  and and_1 (and_1_out, B, Cint);
  and and_2 (and_2_out, A, Cint);
  and and_3 (and_3_out, A, B);
  not not_1 (not_1_out, A);
  not not_2 (not_2_out, B);
  not not_3 (not_3_out, A);
  not not_4 (not_4_out, Cint);
  not not_5 (not_5_out, B);
  not not_6 (not_6_out, Cint);
  or or_1 (Cout, and_1_out, and_2_out, and_3_out);
  and and_4 (and_4_out, not_1_out, not_2_out, Cint);
  and and_5 (and_5_out, not_3_out, B, not_4_out);
  and and_6 (and_6_out, A, not_5_out, not_6_out);
  and and_7 (and_7_out, A, B, Cint);
  or or_2 (S, and_4_out, and_5_out, and_6_out, and_7_out);
endmodule

module somador (
  input  A_prime_prime_prime_prime,
  input  B_prime_prime_prime_prime,
  input  A_prime_prime_prime,
  input  B_prime_prime_prime,
  input  A_prime_prime,
  input  B_prime_prime,
  input  A,
  input  B,
  output Cout,
  output RS4,
  output RS3,
  output RS2,
  output RS1,
  output overflow
);

  wire full_2_cout, full_3_cout, full_4_cout;

  full full_1 (.A(A_prime_prime_prime_prime), .B(B_prime_prime_prime_prime), .Cint(full_2_cout), .Cout(Cout), .S(RS4));
  full full_2 (.A(A_prime_prime_prime), .B(B_prime_prime_prime), .Cint(full_3_cout), .Cout(full_2_cout), .S(RS3));
  full full_3 (.A(A_prime_prime), .B(B_prime_prime), .Cint(full_4_cout), .Cout(full_3_cout), .S(RS2));
  full full_4 (.A(A), .B(B), .Cint(1'b0), .Cout(full_4_cout), .S(RS1));
  xor xor_1 (overflow, full_2_cout, Cout);
endmodule
