// Logisim project b.circ as structural Verilog: 1 circuit, main circuit main
module main (
  input  A,
  input  B,
  input  C,
  input  D,
  output b_2
);

  wire and_1_out, and_2_out, and_3_out, and_4_out, and_5_out;

  and and_1 (and_1_out, A, B);
  and and_2 (and_2_out, ~C, ~D);  // AND_Gate
  and and_3 (and_3_out, ~A, ~B);  // AND_Gate
  and and_4 (and_4_out, ~A, C, D);  // AND_Gate
  and and_5 (and_5_out, A, ~C);  // AND_Gate
  or or_1 (b_2, and_1_out, and_2_out, and_3_out, and_4_out, and_5_out);
endmodule
