// Logisim project circuito somador 2 solo.circ lino (1).circ as structural Verilog: 5 circuits, main circuit main
module main (
  input  [3:0] A,
  input  Cint,
  input  [3:0] B,
  output Cout,
  output out_5,
  output out_6,
  output out_7,
  output out_8,
  output Ov
);

  wire decodificador_1_a, decodificador_1_b, decodificador_1_c, decodificador_1_d, decodificador_1_e,
       decodificador_1_f, decodificador_1_g;

  somador_4_bits somador_4_bits_1 (
    .A4(A[3]), .B4(B[3]), .A3(A[2]), .B3(B[2]), .A2(A[1]), .B2(B[1]), .A1(A[0]), .B1(B[0]), .Cout(Cout),
    .in_9(Cint), .S4(out_5), .S3(out_6), .S2(out_7), .S1(out_8), .ov(Ov));
  decodificador decodificador_1 (
    .S4(out_5), .S3(out_6), .S2(out_7), .S1(out_8), .A(decodificador_1_a), .B(decodificador_1_b),
    .C(decodificador_1_c), .D(decodificador_1_d), .E(decodificador_1_e), .F(decodificador_1_f),
    .G(decodificador_1_g));
  _7_Segment_Display u_7_segment_display_1 (.g(out_5));  // open: f, a, b, e, d, c, dp
  _7_Segment_Display u_7_segment_display_2 (
    .g(decodificador_1_g), .f(decodificador_1_f), .a(decodificador_1_a), .b(decodificador_1_b),
    .e(decodificador_1_e), .d(decodificador_1_d), .c(decodificador_1_c));  // open: dp
endmodule

module Half_adder (
  input  A,
  input  B,
  output Cout,
  output S
);

  and and_1 (Cout, A, B);
  xor xor_1 (S, A, B);
endmodule

module Full_adder (
  input  A,
  input  B,
  input  Cint,
  output Cout,
  output S
);

  wire and_1_out, and_2_out, and_3_out, and_4_out, and_5_out, and_6_out, and_7_out, not_1_out, not_2_out,
       not_3_out, not_4_out, not_5_out, not_6_out;

  and and_1 (and_1_out, B, Cint);
  and and_2 (and_2_out, A, Cint);
  and and_3 (and_3_out, A, B);
  not not_1 (not_1_out, A);
  not not_2 (not_2_out, B);
  not not_3 (not_3_out, A);
  not not_4 (not_4_out, Cint);
  not not_5 (not_5_out, B);
  not not_6 (not_6_out, Cint);
  or or_1 (Cout, and_1_out, and_2_out, and_3_out);
  and and_4 (and_4_out, not_1_out, not_2_out, Cint);
  and and_5 (and_5_out, not_3_out, B, not_4_out);
  and and_6 (and_6_out, A, not_5_out, not_6_out);
  and and_7 (and_7_out, A, B, Cint);
  or or_2 (S, and_4_out, and_5_out, and_6_out, and_7_out);
endmodule

module somador_4_bits (
  input  A4,
  input  B4,
  input  A3,
  input  B3,
  input  A2,
  input  B2,
  input  A1,
  input  B1,
  input  in_9,
  output Cout,
  output S4,
  output S3,
  output S2,
  output S1,
  output ov
);

  wire full_adder_2_cout, full_adder_3_cout, full_adder_4_cout;

  Full_adder full_adder_1 (.A(A4), .B(B4), .Cint(full_adder_2_cout), .Cout(Cout), .S(S4));
  Full_adder full_adder_2 (.A(A3), .B(B3), .Cint(full_adder_3_cout), .Cout(full_adder_2_cout), .S(S3));
  Full_adder full_adder_3 (.A(A2), .B(B2), .Cint(full_adder_4_cout), .Cout(full_adder_3_cout), .S(S2));
  Full_adder full_adder_4 (.A(A1), .B(B1), .Cint(in_9), .Cout(full_adder_4_cout), .S(S1));
  xor xor_1 (ov, Cout, full_adder_2_cout);
endmodule

module decodificador (
  input  S4,
  input  S3,
  input  S2,
  input  S1,
  output A,
  output B,
  output C,
  output D,
  output E,
  output F,
  output G
);

  wire and_1_out, and_2_out, and_3_out, and_4_out, and_5_out, and_6_out, and_7_out, and_8_out, and_9_out,
       and_10_out, and_11_out, and_12_out, and_13_out, and_14_out, and_15_out, and_16_out, and_17_out,
       and_18_out, and_19_out, and_20_out, and_21_out, and_22_out, and_23_out, and_24_out, and_25_out,
       and_26_out, not_1_out, not_2_out, not_3_out, not_4_out, not_5_out, not_6_out, not_7_out, not_8_out,
       not_9_out, not_10_out, not_11_out, not_12_out, not_13_out, not_14_out, not_15_out, not_16_out,
       not_17_out, not_18_out, not_19_out, not_20_out, not_21_out, not_22_out, not_23_out, not_24_out,
       not_25_out, not_26_out, not_27_out, not_28_out, not_29_out, not_30_out, not_31_out, not_32_out,
       not_33_out, not_34_out, not_35_out;

  not not_1 (not_1_out, S3);
  and and_1 (and_1_out, not_1_out, not_2_out);
  not not_2 (not_2_out, S1);
  not not_3 (not_3_out, S4);
  and and_2 (and_2_out, not_3_out, S2);
  and and_3 (and_3_out, S2, not_4_out);
  not not_4 (not_4_out, S1);
  and and_4 (and_4_out, S3, not_5_out, S1);
  not not_5 (not_5_out, S2);
  and and_5 (and_5_out, S4, not_6_out);
  not not_6 (not_6_out, S3);
  not not_7 (not_7_out, S4);
  and and_6 (and_6_out, not_7_out, not_8_out);
  not not_8 (not_8_out, S3);
  not not_9 (not_9_out, S3);
  and and_7 (and_7_out, not_9_out, not_10_out);
  not not_10 (not_10_out, S2);
  not not_11 (not_11_out, S2);
  and and_8 (and_8_out, not_11_out, not_12_out);
  not not_12 (not_12_out, S1);
  not not_13 (not_13_out, S4);
  and and_9 (and_9_out, not_13_out, S2, S1);
  and and_10 (and_10_out, S4, S3);
  not not_14 (not_14_out, S2);
  not not_15 (not_15_out, S4);
  and and_11 (and_11_out, not_15_out, S3);
  and and_12 (and_12_out, S4, not_16_out);
  not not_16 (not_16_out, S3);
  not not_17 (not_17_out, S3);
  and and_13 (and_13_out, not_17_out, not_18_out);
  not not_18 (not_18_out, S1);
  not not_19 (not_19_out, S3);
  and and_14 (and_14_out, not_19_out, S2);
  and and_15 (and_15_out, S2, not_20_out);
  not not_20 (not_20_out, S1);
  and and_16 (and_16_out, S3, not_21_out, S1);
  not not_21 (not_21_out, S2);
  not not_22 (not_22_out, S3);
  and and_17 (and_17_out, not_22_out, not_23_out);
  not not_23 (not_23_out, S1);
  and and_18 (and_18_out, S2, not_24_out);
  not not_24 (not_24_out, S1);
  not not_25 (not_25_out, S2);
  and and_19 (and_19_out, not_25_out, not_26_out);
  not not_26 (not_26_out, S1);
  not not_27 (not_27_out, S4);
  and and_20 (and_20_out, not_27_out, S3, not_28_out);
  not not_28 (not_28_out, S2);
  not not_29 (not_29_out, S4);
  and and_21 (and_21_out, not_29_out, S3, not_30_out);
  not not_30 (not_30_out, S1);
  not not_31 (not_31_out, S3);
  and and_22 (and_22_out, S4, not_31_out, S2);
  not not_32 (not_32_out, S3);
  and and_23 (and_23_out, not_32_out, S2);
  and and_24 (and_24_out, S3, not_33_out);
  not not_33 (not_33_out, S2);
  and and_25 (and_25_out, S3, not_34_out);
  not not_34 (not_34_out, S1);
  and and_26 (and_26_out, S4, not_35_out);
  not not_35 (not_35_out, S1);
  or or_1 (A, and_1_out, and_2_out, and_3_out, and_4_out, and_5_out);
  or or_2 (B, and_6_out, and_7_out, and_8_out, and_9_out, and_10_out);
  or or_3 (C, not_14_out, S1, and_11_out, and_12_out);
  or or_4 (D, and_13_out, and_14_out, and_15_out, and_16_out);
  or or_5 (E, and_17_out, and_18_out);
  or or_6 (F, and_19_out, and_20_out, and_21_out, and_22_out);
  or or_7 (G, and_23_out, and_24_out, and_25_out, and_26_out);
endmodule
