// Logisim project e.circ as structural Verilog: 1 circuit, main circuit main
module main (
  input  B,
  input  C,
  input  D,
  output e
);

  wire and_1_out, and_2_out;

  and and_1 (and_1_out, C, ~D);  // AND_Gate
  and and_2 (and_2_out, ~B, ~D);  // AND_Gate
  or or_1 (e, and_1_out, and_2_out);
endmodule
