// Logisim project f.circ as structural Verilog: 1 circuit, main circuit main
module main (
  input  A,
  input  B,
  input  C,
  input  D,
  output f
);

  wire and_1_out, and_2_out, and_3_out, and_4_out;

  and and_1 (and_1_out, A, ~B, C);  // AND_Gate
  and and_2 (and_2_out, ~A, B, ~C);  // AND_Gate
  and and_3 (and_3_out, ~A, B, ~D);  // AND_Gate
  and and_4 (and_4_out, ~C, ~D);  // AND_Gate
  or or_1 (f, and_1_out, and_2_out, and_3_out, and_4_out);
endmodule
