// Logisim project g.circ as structural Verilog: 1 circuit, main circuit main
module main (
  input  A,
  input  B,
  input  C,
  input  D,
  output g
);

  wire and_1_out, and_2_out, and_3_out, and_4_out;

  and and_1 (and_1_out, A, ~D);  // AND_Gate
  and and_2 (and_2_out, B, ~C);  // AND_Gate
  and and_3 (and_3_out, ~B, C);  // AND_Gate
  and and_4 (and_4_out, C, ~D);  // AND_Gate
  or or_1 (g, and_1_out, and_2_out, and_3_out, and_4_out);
endmodule
