// Logisim project memoria.circ as structural Verilog: 8 circuits, main circuit mux
// reg A
module principal (
  output [7:0] out_1,
  output [3:0] out_2,
  output [3:0] out_3,
  output [3:0] out_4
);

  wire and_1_out, and_2_out, clock_1_out, rom_opcode_operando_1_en_a, rom_opcode_operando_1_en_b,
       rom_opcode_operando_1_s1, rom_opcode_operando_1_s2;
  wire [3:0] mux_1_z, mux_2_z, rom_opcode_operando_1_operando;

  Clock clock_1 (.out(clock_1_out));
  and and_1 (and_1_out, clock_1_out, rom_opcode_operando_1_en_b);
  and and_2 (and_2_out, clock_1_out, rom_opcode_operando_1_en_a);
  registrador reg_B (.in_1(and_1_out), .in_2(out_3), .out_3(out_2));
  registrador reg_A (.in_1(and_2_out), .in_2(out_3), .out_3(out_4));
  rom_opcode_operando rom_opcode_operando_1 (
    .in_1(clock_1_out), .OPERANDO(rom_opcode_operando_1_operando), .out_2(out_1),
    .en_A(rom_opcode_operando_1_en_a), .en_B(rom_opcode_operando_1_en_b), .S1(rom_opcode_operando_1_s1),
    .S2(rom_opcode_operando_1_s2));
  MUX mux_1 (.in_1(rom_opcode_operando_1_s1), .B0(rom_opcode_operando_1_operando), .B1(out_2), .Z(mux_1_z));
  MUX mux_2 (.in_1(rom_opcode_operando_1_s2), .B0(out_4), .B1(4'b0000), .Z(mux_2_z));
  somador somador_1 (
    .A_prime_prime_prime_prime(mux_1_z[3]), .B_prime_prime_prime_prime(mux_2_z[3]),
    .A_prime_prime_prime(mux_1_z[2]), .B_prime_prime_prime(mux_2_z[2]), .A_prime_prime(mux_1_z[1]),
    .B_prime_prime(mux_2_z[1]), .A(mux_1_z[0]), .B(mux_2_z[0]), .out_10(out_3));  // open: Cout, overflow

  // Notes on the sheet:
  //   en_B
  //   en_A
  //   S1
  //   S2
endmodule

module MUX (
  input  in_1,
  input  [3:0] B0,
  input  [3:0] B1,
  output [3:0] Z
);

  mux mux (.S(in_1), .B0(B0[0]), .B1(B1[0]), .out_4(Z[0]));
  mux mux_2 (.S(in_1), .B0(B0[1]), .B1(B1[1]), .out_4(Z[1]));
  mux mux_3 (.S(in_1), .B0(B0[2]), .B1(B1[2]), .out_4(Z[2]));
  mux mux_4 (.S(in_1), .B0(B0[3]), .B1(B1[3]), .out_4(Z[3]));
endmodule

module mux (
  input  S,
  input  B0,
  input  B1,
  output out_4
);

  wire and_1_out, and_2_out, not_1_out;

  not not_1 (not_1_out, S);
  and and_1 (and_1_out, not_1_out, B0);
  and and_2 (and_2_out, S, B1);
  or or_1 (out_4, and_1_out, and_2_out);
endmodule

module registrador (
  input  in_1,
  input  [3:0] in_2,
  output [3:0] out_3
);

  wire not_1_out, not_2_out, not_3_out, not_4_out;

  not not_1 (not_1_out, in_2[0]);
  not not_2 (not_2_out, in_2[1]);
  not not_3 (not_3_out, in_2[2]);
  not not_4 (not_4_out, in_2[3]);
  J_K_Flip_Flop j_k_ff_1 (.J(in_2[0]), .clk(in_1), .K(not_1_out), .Q(out_3[0]));  // open: Qn, preset, en, reset
  J_K_Flip_Flop j_k_ff_2 (.J(in_2[1]), .clk(in_1), .K(not_2_out), .Q(out_3[1]));  // open: Qn, preset, en, reset
  J_K_Flip_Flop j_k_ff_3 (.J(in_2[2]), .clk(in_1), .K(not_3_out), .Q(out_3[2]));  // open: Qn, preset, en, reset
  J_K_Flip_Flop j_k_ff_4 (.J(in_2[3]), .clk(in_1), .K(not_4_out), .Q(out_3[3]));  // open: Qn, preset, en, reset
endmodule

module rom_opcode_operando (
  input  in_1,
  output [7:0] out_2,
  output [3:0] OPERANDO,
  output en_A,
  output en_B,
  output S1,
  output S2
);

  wire [3:0] contador_1_saida;

  contador contador_1 (.saida(contador_1_saida), .in_1(in_1));
  ROM #(.addrWidth(4)) rom_1 (.addr(contador_1_saida), .data({out_2[7:6], en_B, en_A, OPERANDO}));  // open: sel

  assign out_2[5:0] = {en_B, en_A, OPERANDO};
  assign S1 = out_2[6];
  assign S2 = out_2[7];

  // Notes on the sheet:
  //   contents of rom_1 (hex, n*v repeats v):
  //   30 1d 25 d0 ab 93
endmodule

module contador (
  input  in_1,
  output [3:0] saida
);

  wire j_k_ff_1_qn, j_k_ff_2_qn, j_k_ff_3_qn, not_1_out;

  not not_1 (not_1_out, in_1);
  J_K_Flip_Flop j_k_ff_1 (
    .J(1'b1), .clk(not_1_out), .K(1'b1), .Q(saida[0]), .Qn(j_k_ff_1_qn));  // open: preset, en, reset
  J_K_Flip_Flop j_k_ff_2 (
    .J(1'b1), .clk(j_k_ff_1_qn), .K(1'b1), .Q(saida[1]), .Qn(j_k_ff_2_qn));  // open: preset, en, reset
  J_K_Flip_Flop j_k_ff_3 (
    .J(1'b1), .clk(j_k_ff_2_qn), .K(1'b1), .Q(saida[2]), .Qn(j_k_ff_3_qn));  // open: preset, en, reset
  J_K_Flip_Flop j_k_ff_4 (.J(1'b1), .clk(j_k_ff_3_qn), .K(1'b1), .Q(saida[3]));  // open: Qn, preset, en, reset
endmodule

module somador (
  input  A_prime_prime_prime_prime,
  input  B_prime_prime_prime_prime,
  input  A_prime_prime_prime,
  input  B_prime_prime_prime,
  input  A_prime_prime,
  input  B_prime_prime,
  input  A,
  input  B,
  output Cout,
  output [3:0] out_10,
  output overflow
);

  wire full_2_cout, full_3_cout, full_4_cout;

  full full_1 (
    .A(A_prime_prime_prime_prime), .B(B_prime_prime_prime_prime), .Cint(full_2_cout), .Cout(Cout),
    .S(out_10[0]));
  full full_2 (.A(A_prime_prime_prime), .B(B_prime_prime_prime), .Cint(full_3_cout), .Cout(full_2_cout), .S(out_10[1]));
  full full_3 (.A(A_prime_prime), .B(B_prime_prime), .Cint(full_4_cout), .Cout(full_3_cout), .S(out_10[2]));
  full full_4 (.A(A), .B(B), .Cint(1'b0), .Cout(full_4_cout), .S(out_10[3]));
  xor xor_1 (overflow, full_2_cout, Cout);
endmodule

module full (
  input  A,
  input  B,
  input  Cint,
  output Cout,
  output S
);

  wire and_1_out, and_2_out, and_3_out, and_4_out, and_5_out, and_6_out, and_7_out, not_1_out, not_2_out,
       not_3_out, not_4_out, not_5_out, not_6_out;

  and and_1 (and_1_out, B, Cint);
  and and_2 (and_2_out, A, Cint);
  and and_3 (and_3_out, A, B);
  not not_1 (not_1_out, A);
  not not_2 (not_2_out, B);
  not not_3 (not_3_out, A);
  not not_4 (not_4_out, Cint);
  not not_5 (not_5_out, B);
  not not_6 (not_6_out, Cint);
  or or_1 (Cout, and_1_out, and_2_out, and_3_out);
  and and_4 (and_4_out, not_1_out, not_2_out, Cint);
  and and_5 (and_5_out, not_3_out, B, not_4_out);
  and and_6 (and_6_out, A, not_5_out, not_6_out);
  and and_7 (and_7_out, A, B, Cint);
  or or_2 (S, and_4_out, and_5_out, and_6_out, and_7_out);
endmodule
