// Logisim project memoria_e_mux.circ as structural Verilog: 1 circuit, main circuit main
module main (
  input  in_1
);

  wire clock_1_out, not_1_out, undriven;
  wire [3:0] adder_1_out, multiplexer_1_out, multiplexer_2_out, RA_q, RB_q;
  wire [7:0] counter_1_q, rom_1_data;

  Counter counter_1 (.Q(counter_1_q), .clk(not_1_out), .clr(in_1));  // open: load, D, count, carry
  not not_1 (not_1_out, clock_1_out);
  Clock clock_1 (.out(clock_1_out));
  ROM rom_1 (.addr(counter_1_q), .data(rom_1_data), .sel(undriven));
  Register #(.width(4)) RA (.D(adder_1_out), .en(rom_1_data[7]), .Q(RA_q), .clk(clock_1_out), .clr(in_1));
  Register #(.width(4)) RB (.D(adder_1_out), .en(rom_1_data[6]), .Q(RB_q), .clk(clock_1_out), .clr(in_1));
  Multiplexer #(.width(4), .enable("false")) multiplexer_1 (
    .in0(rom_1_data[3:0]), .in1(RA_q), .out(multiplexer_1_out), .sel(rom_1_data[5]));
  Multiplexer #(.width(4)) multiplexer_2 (
    .in0(4'b0000), .in1(RB_q), .out(multiplexer_2_out), .sel(rom_1_data[4]));  // open: en
  Adder #(.width(4)) adder_1 (.a(multiplexer_1_out), .b(multiplexer_2_out), .out(adder_1_out));  // open: cin, cout

  // Notes on the sheet:
  //   contents of rom_1 (hex, n*v repeats v):
  //   f2 75 5e
endmodule
